# Fritzing sketch BoomBox (saved by Fritzing 0.9.6b)
breadboards: 1

parts:
  Part1 = Arduino Uno (Rev3)
  S1 = Pushbutton [package="[THT]"]
  S2 = Pushbutton [package="[THT]"]
  S3 = Pushbutton [package="[THT]"]
  S4 = Pushbutton [package="[THT]"]
  S5 = Pushbutton [package="[THT]"]
  S6 = Pushbutton [package="[THT]"]
  Part2 = Arduino MP3 Player Shield

nets:
  N1: Part1.A0, S6.Pin_3, S6.Pin_4
  N2: Part1.A1, S5.Pin_3, S5.Pin_4
  N3: Part1.A2, S4.Pin_3, S4.Pin_4
  N4: Part1.A3, S3.Pin_3, S3.Pin_4
  N5: Part1.A4/SDA, S2.Pin_3, S2.Pin_4
  N6: Part1.A5/SCL, S1.Pin_3, S1.Pin_4
  N7: Part1.D8, Part2.5V-MP3-RST
  N8: Part1.D9_PWM, Part2.5V-SD-CS
  N9: Part1.D11_PWM/MOSI, Part2.5V-MOSI
  N10: Part1.D12/MISO, Part2.MISO
  N11: Part1.D13/SCK, Part2.5V-SCK
  N12: Part1.D2, Part2.MP3-DREQ
  N13: Part1.D6_PWM, Part2.5V-MP3-CS
  N14: Part1.D7, Part2.5V-MP3-DCS
  N15: Part1.GND, S1.Pin_1, S1.Pin_2, S2.Pin_1, S2.Pin_2, S3.Pin_1, S3.Pin_2, S4.Pin_1, S4.Pin_2, S5.Pin_1, S5.Pin_2, S6.Pin_1, S6.Pin_2
